// Logisim project bonkpu.circ as structural Verilog: 1 circuit, main circuit main
module main (
);

  wire [7:0] microcode_a_data, microcode_c_data;
  wire [14:0] dipswitch_1_sw15;
  wire [15:8] microcode_b_data;

  DipSwitch #(.number(15)) dipswitch_1 (
    .sw1(dipswitch_1_sw15[14]), .sw2(dipswitch_1_sw15[13]), .sw3(dipswitch_1_sw15[12]),
    .sw4(dipswitch_1_sw15[11]), .sw5(dipswitch_1_sw15[10]), .sw6(dipswitch_1_sw15[9]),
    .sw7(dipswitch_1_sw15[8]), .sw8(dipswitch_1_sw15[7]), .sw9(dipswitch_1_sw15[6]),
    .sw10(dipswitch_1_sw15[5]), .sw11(dipswitch_1_sw15[4]), .sw12(dipswitch_1_sw15[3]),
    .sw13(dipswitch_1_sw15[2]), .sw14(dipswitch_1_sw15[1]), .sw15(dipswitch_1_sw15[0]));
  ROM #(.addrWidth(15)) microcode_a (.addr(dipswitch_1_sw15), .data(microcode_a_data));
  ROM #(.addrWidth(15)) microcode_b (.addr(dipswitch_1_sw15), .data(microcode_b_data));
  ROM #(.addrWidth(15)) microcode_c (.addr(dipswitch_1_sw15), .data(microcode_c_data));
  LedBar #(.matrixcols(24)) ledbar_1 (
    .led0(microcode_a_data[7]), .led1(microcode_a_data[6]), .led2(microcode_a_data[5]),
    .led3(microcode_a_data[4]), .led4(microcode_a_data[3]), .led5(microcode_a_data[2]),
    .led6(microcode_a_data[1]), .led7(microcode_a_data[0]), .led8(microcode_b_data[15]),
    .led9(microcode_b_data[14]), .led10(microcode_b_data[13]), .led11(microcode_b_data[12]),
    .led12(microcode_b_data[11]), .led13(microcode_b_data[10]), .led14(microcode_b_data[9]),
    .led15(microcode_b_data[8]), .led16(microcode_c_data[7]), .led17(microcode_c_data[6]),
    .led18(microcode_c_data[5]), .led19(microcode_c_data[4]), .led20(microcode_c_data[3]),
    .led21(microcode_c_data[2]), .led22(microcode_c_data[1]), .led23(microcode_c_data[0]));

  // Notes on the sheet:
  //   contents of microcode_a (hex, n*v repeats v):
  //   40 20 c 13*0 40 20 c 0 40 20 9 9*0 40 20 c 0 40 20 8 40 20 8 6*0 40 20 c 13*0 40 20 c 0 40 20 8 40
  //   20 8 6*0 40 20 c 13*0 40 20 c 0 40 20 8 40 20 8 6*0 40 20 c 13*0 40 20 c 0 40 20 8 40 20 8 6*0 40 20
  //   c 13*0 40 20 c 0 40 20 8 40 20 8 6*0 40 20 c 13*0 40 20 c 13*0 40 20 c 13*0 40 20 c 13*0 40 20 c
  //   13*0 40 20 c 13*0 40 20 c 13*0 40 20 c 13*0 40 20 c 13*0 40 20 c 13*0 40 20 c 13*0 40 20 c 13*0 40
  //   20 c 13*0 40 20 c 13*0 40 20 c 13*0 40 20 c 13*0 40 20 c 13*0 40 20 c 13*0 40 20 c 13*0 40 20 c 13*0
  //   40 20 c 13*0 40 20 c 13*0 40 20 c 13*0 40 20 c 13*0 40 20 c 13*0 40 20 c 13*0 40 20 c 13*0 40 20 c
  //   13*0 40 20 c 13*0 40 20 c 13*0 40 20 c 13*0 40 20 c 13*0 40 20 c 13*0 40 20 c 13*0 40 20 c 13*0 40
  //   20 c 13*0 40 20 c 13*0 40 20 c 13*0 40 20 c 13*0 40 20 c 13*0 40 20 c 13*0 40 20 c 13*0 40 20 c 13*0
  //   40 20 c 13*0 40 20 c 13*0 40 20 c 13*0 40 20 c 13*0 40 20 c 13*0 40 20 c 13*0 40 20 c 13*0 40 20 c
  //   13*0 40 20 c 13*0 40 20 c 13*0 40 20 c 13*0 40 20 c 13*0 40 20 c 13*0 40 20 c 13*0 40 20 c 13*0 40
  //   20 c 13*0 40 20 c 13*0 40 20 c 13*0 40 20 c 13*0 40 20 c 13*0 40 20 c 13*0 40 20 c 13*0 40 20 c 13*0
  //   40 20 c 13*0 40 20 c 13*0 40 20 c 13*0 40 20 c 13*0 40 20 c 13*0 40 20 c 13*0 40 20 c 13*0 40 20 c
  //   13*0 40 20 c 13*0 40 20 c 13*0 40 20 c 13*0 40 20 c 13*0 40 20 c 13*0 40 20 c 13*0 40 20 c 13*0 40
  //   20 c 13*0 40 20 c 13*0 40 20 c 13*0 40 20 c 13*0 40 20 c 13*0 40 20 c 13*0 40 20 c 13*0 40 20 c 13*0
  //   40 20 c 13*0 40 20 c 13*0 40 20 c 13*0 40 20 c 13*0 40 20 c 13*0 40 20 c 13*0 40 20 c 13*0 40 20 c
  //   13*0 40 20 c 13*0 40 20 c 13*0 40 20 c 13*0 40 20 c 13*0 40 20 c 13*0 40 20 c 13*0 40 20 c 13*0 40
  //   20 c 13*0 40 20 c 13*0 40 20 c 13*0 40 20 c 13*0 40 20 c 13*0 40 20 c 13*0 40 20 c 13*0 40 20 c 13*0
  //   40 20 c 13*0 40 20 c 13*0 40 20 c 13*0 40 20 c 13*0 40 20 c 13*0 40 20 c 13*0 40 20 c 13*0 40 20 c
  //   13*0 40 20 c 13*0 40 20 c 13*0 40 20 c 13*0 40 20 c 13*0 40 20 c 13*0 40 20 c 13*0 40 20 c 13*0 40
  //   20 c 13*0 40 20 c 13*0 40 20 c 13*0 40 20 c 13*0 40 20 c 13*0 40 20 c 13*0 40 20 c 13*0 40 20 c 13*0
  //   40 20 c 13*0 40 20 c 13*0 40 20 c 13*0 40 20 c 13*0 40 20 c 13*0 40 20 c 13*0 40 20 c 13*0 40 20 c
  //   13*0 40 20 c 13*0 40 20 c 13*0 40 20 c 13*0 40 20 c 13*0 40 20 c 13*0 40 20 c 13*0 40 20 c 13*0 40
  //   20 c 13*0 40 20 c 13*0 40 20 c 13*0 40 20 c 13*0 40 20 c 13*0 40 20 c 13*0 40 20 c 13*0 40 20 c 13*0
  //   40 20 c 13*0 40 20 c 13*0 40 20 c 13*0 40 20 c 13*0 40 20 c 13*0 40 20 c 13*0 40 20 c 13*0 40 20 c
  //   13*0 40 20 c 13*0 40 20 c 13*0 40 20 c 13*0 40 20 c 13*0 40 20 c 13*0 40 20 c 13*0 40 20 c 13*0 40
  //   20 c 13*0 40 20 c 13*0 40 20 c 13*0 40 20 c 13*0 40 20 c 13*0 40 20 c 13*0 40 20 c 13*0 40 20 c 13*0
  //   40 20 c 13*0 40 20 c 13*0 40 20 c 13*0 40 20 c 13*0 40 20 c 13*0 40 20 c 13*0 40 20 c 13*0 40 20 c
  //   13*0 40 20 c 13*0 40 20 c 13*0 40 20 c 13*0 40 20 c 13*0 40 20 c 13*0 40 20 c 13*0 40 20 c 13*0 40
  //   20 c 13*0 40 20 c 13*0 40 20 c 13*0 40 20 c 13*0 40 20 c 13*0 40 20 c 13*0 40 20 c 13*0 40 20 c 13*0
  //   40 20 c 13*0 40 20 c 13*0 40 20 c 13*0 40 20 c 13*0 40 20 c 13*0 40 20 c 13*0 40 20 c 13*0 40 20 c
  //   13*0 40 20 c 13*0 40 20 c 13*0 40 20 c 13*0 40 20 c 13*0 40 20 c 13*0 40 20 c 13*0 40 20 c 13*0 40
  //   20 c 13*0 40 20 c 13*0 40 20 c 13*0 40 20 c 13*0 40 20 c 13*0 40 20 c 13*0 40 20 c 13*0 40 20 c 13*0
  //   40 20 c 13*0 40 20 c 13*0 40 20 c 13*0 40 20 c 13*0 40 20 c 13*0 40 20 c 13*0 40 20 c 13*0 40 20 c
  //   13*0 40 20 c 13*0 40 20 c 13*0 40 20 c 13*0 40 20 c 13*0 40 20 c 13*0 40 20 c 13*0 40 20 c 13*0 40
  //   20 c 13*0 40 20 c 13*0 40 20 c 13*0 40 20 c 13*0 40 20 c 0 40 20 9 9*0 40 20 c 0 40 20 8 40 20 8 6*0
  //   40 20 c 0 40 20 8 40 20 8 6*0 40 20 c 13*0 40 20 c 13*0 40 20 c 0 40 20 8 40 20 8 6*0 40 20 c 13*0
  //   40 20 c 0 40 20 8 40 20 8 6*0 40 20 c 13*0 40 20 c 0 40 20 8 40 20 8 6*0 40 20 c 13*0 40 20 c 13*0
  //   40 20 c 13*0 40 20 c 13*0 40 20 c 13*0 40 20 c 13*0 40 20 c 13*0 40 20 c 13*0 40 20 c 13*0 40 20 c
  //   13*0 40 20 c 13*0 40 20 c 13*0 40 20 c 13*0 40 20 c 13*0 40 20 c 13*0 40 20 c 13*0 40 20 c 13*0 40
  //   20 c 13*0 40 20 c 13*0 40 20 c 13*0 40 20 c 13*0 40 20 c 13*0 40 20 c 13*0 40 20 c 13*0 40 20 c 13*0
  //   40 20 c 13*0 40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
  //   contents of microcode_b (hex, n*v repeats v):
  //   0 0 2 2 14*0 2 2 1 0 2 11*0 2 2 1 0 42 1 0 2 20 7*0 4*2 12*0 2 2 1 0 42 1 0 2 20 7*0 4*2 12*0 2 2 1
  //   0 42 1 0 2 20 7*0 4*2 12*0 2 2 1 0 42 1 0 2 20 7*0 4*2 12*0 2 2 1 0 42 1 0 2 20 7*0 2 2 14*0 2 2
  //   14*0 2 2 14*0 2 2 14*0 2 2 14*0 2 2 14*0 2 2 14*0 2 2 14*0 2 2 14*0 2 2 14*0 2 2 14*0 2 2 14*0 2 2
  //   14*0 2 2 14*0 2 2 14*0 2 2 14*0 2 2 14*0 2 2 14*0 2 2 14*0 2 2 14*0 2 2 14*0 2 2 14*0 2 2 14*0 2 2
  //   14*0 2 2 14*0 2 2 14*0 2 2 14*0 2 2 14*0 2 2 14*0 2 2 14*0 2 2 14*0 2 2 14*0 2 2 14*0 2 2 14*0 2 2
  //   14*0 2 2 14*0 2 2 14*0 2 2 14*0 2 2 14*0 2 2 14*0 2 2 14*0 2 2 14*0 2 2 14*0 2 2 14*0 2 2 14*0 2 2
  //   14*0 2 2 14*0 2 2 14*0 2 2 14*0 2 2 14*0 2 2 14*0 2 2 14*0 2 2 14*0 2 2 14*0 2 2 14*0 2 2 14*0 2 2
  //   14*0 2 2 14*0 2 2 14*0 2 2 14*0 2 2 14*0 2 2 14*0 2 2 14*0 2 2 14*0 2 2 14*0 2 2 14*0 2 2 14*0 2 2
  //   14*0 2 2 14*0 2 2 14*0 2 2 14*0 2 2 14*0 2 2 14*0 2 2 14*0 2 2 14*0 2 2 14*0 2 2 14*0 2 2 14*0 2 2
  //   14*0 2 2 14*0 2 2 14*0 2 2 14*0 2 2 14*0 2 2 14*0 2 2 14*0 2 2 14*0 2 2 14*0 2 2 14*0 2 2 14*0 2 2
  //   14*0 2 2 14*0 2 2 14*0 2 2 14*0 2 2 14*0 2 2 14*0 2 2 14*0 2 2 14*0 2 2 14*0 2 2 14*0 2 2 14*0 2 2
  //   14*0 2 2 14*0 2 2 14*0 2 2 14*0 2 2 14*0 2 2 14*0 2 2 14*0 2 2 14*0 2 2 14*0 2 2 14*0 2 2 14*0 2 2
  //   14*0 2 2 14*0 2 2 14*0 2 2 14*0 2 2 14*0 2 2 14*0 2 2 14*0 2 2 14*0 2 2 14*0 2 2 14*0 2 2 14*0 2 2
  //   14*0 2 2 14*0 2 2 14*0 2 2 14*0 2 2 14*0 2 2 14*0 2 2 14*0 2 2 14*0 2 2 14*0 2 2 14*0 2 2 14*0 2 2
  //   14*0 2 2 14*0 2 2 14*0 2 2 14*0 2 2 14*0 2 2 14*0 2 2 14*0 2 2 14*0 2 2 14*0 2 2 14*0 2 2 14*0 2 2
  //   14*0 2 2 14*0 2 2 14*0 2 2 14*0 2 2 14*0 2 2 14*0 2 2 14*0 2 2 14*0 2 2 14*0 2 2 14*0 2 2 14*0 2 2
  //   14*0 2 2 14*0 2 2 14*0 2 2 14*0 2 2 14*0 2 2 14*0 2 2 14*0 2 2 14*0 2 2 14*0 2 2 14*0 2 2 14*0 2 2
  //   14*0 2 2 14*0 2 2 14*0 2 2 14*0 2 2 14*0 2 2 14*0 2 2 14*0 2 2 14*0 2 2 14*0 2 2 14*0 2 2 14*0 2 2
  //   14*0 2 2 14*0 2 2 14*0 2 2 14*0 2 2 14*0 2 2 14*0 2 2 14*0 2 2 14*0 2 2 14*0 2 2 14*0 2 2 14*0 2 2
  //   14*0 2 2 14*0 2 2 14*0 2 2 14*0 2 2 14*0 2 2 14*0 2 2 14*0 2 2 14*0 2 2 14*0 2 2 14*0 2 2 14*0 2 2
  //   14*0 2 2 14*0 2 2 14*0 2 2 14*0 2 2 14*0 2 2 14*0 2 2 14*0 2 2 14*0 2 2 14*0 2 2 14*0 2 2 14*0 2 2
  //   14*0 2 2 14*0 2 2 14*0 2 2 14*0 2 2 14*0 2 2 14*0 2 2 14*0 2 2 14*0 2 2 14*0 2 2 14*0 2 2 14*0 2 2
  //   14*0 2 2 14*0 2 2 14*0 2 2 14*0 2 2 14*0 2 2 14*0 2 2 14*0 2 2 14*0 2 2 14*0 2 2 14*0 2 2 14*0 2 2
  //   14*0 2 2 14*0 2 2 14*0 2 2 14*0 2 2 14*0 2 2 14*0 2 2 14*0 2 2 14*0 2 2 14*0 2 2 14*0 2 2 14*0 2 2
  //   14*0 2 2 14*0 2 2 14*0 2 2 1 0 2 11*0 2 2 1 0 42 1 0 2 20 7*0 2 2 1 0 42 1 0 2 20 7*0 4*2 12*0 4*2
  //   12*0 2 2 1 0 42 1 0 2 20 7*0 4*2 12*0 2 2 1 0 42 1 0 2 20 7*0 4*2 12*0 2 2 1 0 42 1 0 2 20 7*0 2 2
  //   14*0 2 2 14*0 2 2 14*0 2 2 14*0 2 2 14*0 2 2 14*0 2 2 14*0 2 2 14*0 2 2 14*0 2 2 14*0 2 2 14*0 2 2
  //   14*0 2 2 14*0 2 2 14*0 2 2 14*0 2 2 14*0 2 2 14*0 2 2 14*0 2 2 14*0 2 2 14*0 2 2 14*0 2 2 14*0 2 2
  //   14*0 2 2 14*0 2 2 14*0 2 2 14*0 2 2 14*0 2 2 14*0 2 2 14*0 2 2 14*0 2 2 14*0 2 2 14*0 2 2 14*0 2 2
  //   14*0 2 2 14*0 2 2 14*0 2 2 14*0 2 2 14*0 2 2 14*0 2 2 14*0 2 2 14*0 2 2 14*0 2 2 14*0 2 2 14*0 2 2
  //   14*0 2 2 14*0 2 2 14*0 2 2 14*0 2 2 14*0 2 2 14*0 2 2 14*0 2 2 14*0 2 2 14*0 2 2 14*0 2 2 14*0 2 2
  //   14*0 2 2 14*0 2 2 14*0 2 2 14*0 2 2 14*0 2 2 14*0 2 2 14*0 2 2 14*0 2 2 14*0 2 2 14*0 2 2 14*0 2 2
  //   14*0 2 2 14*0 2 2 14*0 2 2 14*0 2 2 14*0 2 2 14*0 2 2 14*0 2 2 14*0 2 2 14*0 2 2 14*0 2 2 14*0 2 2
  //   14*0 2 2 14*0 2 2 14*0 2 2 14*0 2 2 14*0 2 2 14*0 2 2 14*0 2 2 14*0 2 2 14*0 2 2 14*0 2 2 14*0 2 2
  //   14*0 2 2 14*0 2 2 14*0 2 2 14*0 2 2 14*0 2 2 14*0 2 2 14*0 2 2 14*0 2 2 14*0 2 2 14*0 2 2 14*0 2 2
  //   14*0 2 2 14*0 2 2 14*0 2 2 14*0 2 2 14*0 2 2 14*0 2 2 14*0 2 2 14*0 2 2 14*0 2 2 14*0 2 2 14*0 2 2
  //   14*0 2 2 14*0 2 2 14*0 2 2 14*0 2 2 14*0 2 2 14*0 2 2 14*0 2 2 14*0 2 2 14*0 2 2 14*0 2 2 14*0 2 2
  //   14*0 2 2 14*0 2 2 14*0 2 2 14*0 2 2 14*0 2 2 14*0 2 2 14*0 2 2 14*0 2 2 14*0 2 2 14*0 2 2 14*0 2 2
  //   14*0 2 2 14*0 2 2 14*0 2 2 14*0 2 2 14*0 2 2 14*0 2 2 14*0 2 2 14*0 2 2 14*0 2 2 14*0 2 2 14*0 2 2
  //   14*0 2 2 14*0 2 2 14*0 2 2 14*0 2 2 14*0 2 2 14*0 2 2 14*0 2 2 14*0 2 2 14*0 2 2 14*0 2 2 14*0 2 2
  //   14*0 2 2 14*0 2 2 14*0 2 2 14*0 2 2 14*0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
  //   contents of microcode_c (hex, n*v repeats v):
  //   40 20 0 1 12*0 40 20 0 0 0 80 1 9*0 40 20 0 0 0 80 0 0 80 40 21 5*0 40 20 0 0 0 1 10*0 40 20 0 0 0
  //   80 0 0 80 40 21 5*0 40 20 0 0 0 1 10*0 40 20 0 0 0 80 0 0 80 40 21 5*0 40 20 0 0 0 1 10*0 40 20 0 0
  //   0 80 0 0 80 40 21 5*0 40 20 0 0 0 1 10*0 40 20 0 0 0 80 0 0 80 40 21 5*0 40 20 0 1 12*0 40 20 0 1
  //   12*0 40 20 0 1 12*0 40 20 0 1 12*0 40 20 0 1 12*0 40 20 0 1 12*0 40 20 0 1 12*0 40 20 0 1 12*0 40 20
  //   0 1 12*0 40 20 0 1 12*0 40 20 0 1 12*0 40 20 0 1 12*0 40 20 0 1 12*0 40 20 0 1 12*0 40 20 0 1 12*0
  //   40 20 0 1 12*0 40 20 0 1 12*0 40 20 0 1 12*0 40 20 0 1 12*0 40 20 0 1 12*0 40 20 0 1 12*0 40 20 0 1
  //   12*0 40 20 0 1 12*0 40 20 0 1 12*0 40 20 0 1 12*0 40 20 0 1 12*0 40 20 0 1 12*0 40 20 0 1 12*0 40 20
  //   0 1 12*0 40 20 0 1 12*0 40 20 0 1 12*0 40 20 0 1 12*0 40 20 0 1 12*0 40 20 0 1 12*0 40 20 0 1 12*0
  //   40 20 0 1 12*0 40 20 0 1 12*0 40 20 0 1 12*0 40 20 0 1 12*0 40 20 0 1 12*0 40 20 0 1 12*0 40 20 0 1
  //   12*0 40 20 0 1 12*0 40 20 0 1 12*0 40 20 0 1 12*0 40 20 0 1 12*0 40 20 0 1 12*0 40 20 0 1 12*0 40 20
  //   0 1 12*0 40 20 0 1 12*0 40 20 0 1 12*0 40 20 0 1 12*0 40 20 0 1 12*0 40 20 0 1 12*0 40 20 0 1 12*0
  //   40 20 0 1 12*0 40 20 0 1 12*0 40 20 0 1 12*0 40 20 0 1 12*0 40 20 0 1 12*0 40 20 0 1 12*0 40 20 0 1
  //   12*0 40 20 0 1 12*0 40 20 0 1 12*0 40 20 0 1 12*0 40 20 0 1 12*0 40 20 0 1 12*0 40 20 0 1 12*0 40 20
  //   0 1 12*0 40 20 0 1 12*0 40 20 0 1 12*0 40 20 0 1 12*0 40 20 0 1 12*0 40 20 0 1 12*0 40 20 0 1 12*0
  //   40 20 0 1 12*0 40 20 0 1 12*0 40 20 0 1 12*0 40 20 0 1 12*0 40 20 0 1 12*0 40 20 0 1 12*0 40 20 0 1
  //   12*0 40 20 0 1 12*0 40 20 0 1 12*0 40 20 0 1 12*0 40 20 0 1 12*0 40 20 0 1 12*0 40 20 0 1 12*0 40 20
  //   0 1 12*0 40 20 0 1 12*0 40 20 0 1 12*0 40 20 0 1 12*0 40 20 0 1 12*0 40 20 0 1 12*0 40 20 0 1 12*0
  //   40 20 0 1 12*0 40 20 0 1 12*0 40 20 0 1 12*0 40 20 0 1 12*0 40 20 0 1 12*0 40 20 0 1 12*0 40 20 0 1
  //   12*0 40 20 0 1 12*0 40 20 0 1 12*0 40 20 0 1 12*0 40 20 0 1 12*0 40 20 0 1 12*0 40 20 0 1 12*0 40 20
  //   0 1 12*0 40 20 0 1 12*0 40 20 0 1 12*0 40 20 0 1 12*0 40 20 0 1 12*0 40 20 0 1 12*0 40 20 0 1 12*0
  //   40 20 0 1 12*0 40 20 0 1 12*0 40 20 0 1 12*0 40 20 0 1 12*0 40 20 0 1 12*0 40 20 0 1 12*0 40 20 0 1
  //   12*0 40 20 0 1 12*0 40 20 0 1 12*0 40 20 0 1 12*0 40 20 0 1 12*0 40 20 0 1 12*0 40 20 0 1 12*0 40 20
  //   0 1 12*0 40 20 0 1 12*0 40 20 0 1 12*0 40 20 0 1 12*0 40 20 0 1 12*0 40 20 0 1 12*0 40 20 0 1 12*0
  //   40 20 0 1 12*0 40 20 0 1 12*0 40 20 0 1 12*0 40 20 0 1 12*0 40 20 0 1 12*0 40 20 0 1 12*0 40 20 0 1
  //   12*0 40 20 0 1 12*0 40 20 0 1 12*0 40 20 0 1 12*0 40 20 0 1 12*0 40 20 0 1 12*0 40 20 0 1 12*0 40 20
  //   0 1 12*0 40 20 0 1 12*0 40 20 0 1 12*0 40 20 0 1 12*0 40 20 0 1 12*0 40 20 0 1 12*0 40 20 0 1 12*0
  //   40 20 0 1 12*0 40 20 0 1 12*0 40 20 0 1 12*0 40 20 0 1 12*0 40 20 0 1 12*0 40 20 0 1 12*0 40 20 0 1
  //   12*0 40 20 0 1 12*0 40 20 0 1 12*0 40 20 0 1 12*0 40 20 0 1 12*0 40 20 0 1 12*0 40 20 0 1 12*0 40 20
  //   0 1 12*0 40 20 0 1 12*0 40 20 0 1 12*0 40 20 0 1 12*0 40 20 0 1 12*0 40 20 0 1 12*0 40 20 0 1 12*0
  //   40 20 0 1 12*0 40 20 0 1 12*0 40 20 0 1 12*0 40 20 0 1 12*0 40 20 0 1 12*0 40 20 0 1 12*0 40 20 0 1
  //   12*0 40 20 0 1 12*0 40 20 0 1 12*0 40 20 0 1 12*0 40 20 0 1 12*0 40 20 0 1 12*0 40 20 0 1 12*0 40 20
  //   0 1 12*0 40 20 0 1 12*0 40 20 0 1 12*0 40 20 0 1 12*0 40 20 0 1 12*0 40 20 0 1 12*0 40 20 0 1 12*0
  //   40 20 0 1 12*0 40 20 0 1 12*0 40 20 0 1 12*0 40 20 0 1 12*0 40 20 0 1 12*0 40 20 0 1 12*0 40 20 0 1
  //   12*0 40 20 0 1 12*0 40 20 0 1 12*0 40 20 0 1 12*0 40 20 0 1 12*0 40 20 0 1 12*0 40 20 0 1 12*0 40 20
  //   0 1 12*0 40 20 0 1 12*0 40 20 0 1 12*0 40 20 0 1 12*0 40 20 0 1 12*0 40 20 0 1 12*0 40 20 0 1 12*0
  //   40 20 0 1 12*0 40 20 0 1 12*0 40 20 0 1 12*0 40 20 0 1 12*0 40 20 0 1 12*0 40 20 0 1 12*0 40 20 0 1
  //   12*0 40 20 0 1 12*0 40 20 0 1 12*0 40 20 0 1 12*0 40 20 0 1 12*0 40 20 0 1 12*0 40 20 0 1 12*0 40 20
  //   0 1 12*0 40 20 0 1 12*0 40 20 0 1 12*0 40 20 0 1 12*0 40 20 0 1 12*0 40 20 0 1 12*0 40 20 0 1 12*0
  //   40 20 0 1 12*0 40 20 0 1 12*0 40 20 0 1 12*0 40 20 0 1 12*0 40 20 0 1 12*0 40 20 0 1 12*0 40 20 0 1
  //   12*0 40 20 0 1 12*0 40 20 0 1 12*0 40 20 0 1 12*0 40 20 0 1 12*0 40 20 0 0 0 80 1 9*0 40 20 0 0 0 80
  //   0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
endmodule
